# Fritzing sketch Wiring (saved by Fritzing 0.9.3b)

parts:
  S1 = H-Bridge with L298N
  Raspberry_Pi_1 = Raspberry Pi 4 [part_number=RPI-4-b]  # not connected
  Part1 = Arduino Mega 2560 (Rev3)  # not connected
  M1 = DC Motor
  M2 = DC Motor

nets:
  N1: S1.M1-01, M1.pin_2
  N2: S1.M1-02, M1.pin_1
  N3: S1.M2-01, M2.pin_2
  N4: S1.M2-02, M2.pin_1

custom parts:
  H-Bridge with L298N: h-bridge
  Raspberry Pi 4: The RPi4, a faster version of the awesome Raspberry Pi 2 B ARM Board with 40 pin gpio. Ready for special Raspberry Pi B+ and RPi2 Hat (Hardware attached (on) top)
